// Logisim project ALU16.circ as structural Verilog: 35 circuits, main circuit main
module main (
  input  in_1,
  output out_2
);

  NOT not_1 (.X(in_1), .X_prime(out_2));
endmodule

module NOT (
  input  X,
  output X_prime
);

  wire transistor_1_out, undriven;

  Transistor transistor_1 (.in(1'b1), .out(transistor_1_out), .gate(undriven));
  Transistor #(.\type ("n")) transistor_2 (.in(1'b0), .out(transistor_1_out), .gate(undriven));
  not not_1 (X_prime, X);

  // Notes on the sheet:
  //   X: pull=down
endmodule

module NAND (
  input  A,
  input  B,
  output Y__AB__prime
);

  wire transistor_3_out;

  Transistor transistor_1 (.in(1'b1), .out(Y__AB__prime), .gate(A));
  Transistor #(.\type ("n")) transistor_2 (.in(transistor_3_out), .out(Y__AB__prime), .gate(A));
  Transistor #(.\type ("n")) transistor_3 (.in(1'b0), .out(transistor_3_out), .gate(B));
  Transistor transistor_4 (.in(1'b1), .out(Y__AB__prime), .gate(B));
endmodule

module NOR (
  input  A,
  input  B,
  output Y___A_B__prime
);

  wire transistor_1_out;

  Transistor transistor_1 (.in(1'b1), .out(transistor_1_out), .gate(A));
  Transistor transistor_2 (.in(transistor_1_out), .out(Y___A_B__prime), .gate(B));
  Transistor #(.\type ("n")) transistor_3 (.in(1'b0), .out(Y___A_B__prime), .gate(A));
  Transistor #(.\type ("n")) transistor_4 (.in(1'b0), .out(Y___A_B__prime), .gate(B));
endmodule

module XOR (
  input  A,
  input  B,
  output Y_XOR
);

  wire not_1_x_prime, not_2_x_prime;

  NOT not_1 (.X(A), .X_prime(not_1_x_prime));
  NOT not_2 (.X(B), .X_prime(not_2_x_prime));
  xor xor_1 (Y_XOR, B, A);
  Transistor transistor_1 ();  // open: in, out, gate
endmodule

module FA (
  input  A,
  input  B,
  input  Cin,
  output S,
  output Cout
);

  wire and_1_out, and_2_out, xor_1_out;

  xor xor_1 (xor_1_out, A, B);
  xor xor_2 (S, xor_1_out, Cin);
  and and_1 (and_1_out, Cin, xor_1_out);
  and and_2 (and_2_out, A, B);
  or or_1 (Cout, and_1_out, and_2_out);

  // Notes on the sheet:
  //   Cin: pull=down
  //   A: pull=down
  //   B: pull=down
endmodule

module FA4 (
  input  B3,
  input  B2,
  input  B1,
  input  B0,
  input  A3,
  input  A2,
  input  A1,
  input  A0,
  input  Cin,
  output Cout,
  output S3,
  output S2,
  output S1,
  output S0
);

  wire fa_2_cout, fa_3_cout, fa_4_cout;

  FA fa_1 (.A(A3), .B(B3), .Cin(fa_2_cout), .S(S3), .Cout(Cout));
  FA fa_2 (.A(A2), .B(B2), .Cin(fa_3_cout), .S(S2), .Cout(fa_2_cout));
  FA fa_3 (.A(A1), .B(B1), .Cin(fa_4_cout), .S(S1), .Cout(fa_3_cout));
  FA fa_4 (.A(A0), .B(B0), .Cin(Cin), .S(S0), .Cout(fa_4_cout));
endmodule

module Sum16 (
  input  [15:0] A,
  input  [15:0] in_2,
  output Cout,
  output [15:0] out_4
);

  wire fa4_2_cout, fa4_3_cout, fa4_4_cout;

  FA4 fa4_1 (
    .Cout(Cout), .Cin(fa4_2_cout), .B3(in_2[15]), .B2(in_2[14]), .B1(in_2[13]), .B0(in_2[12]), .A3(A[15]),
    .A2(A[14]), .A1(A[13]), .A0(A[12]), .S3(out_4[15]), .S2(out_4[14]), .S1(out_4[13]), .S0(out_4[12]));
  FA4 fa4_2 (
    .Cout(fa4_2_cout), .Cin(fa4_3_cout), .B3(in_2[11]), .B2(in_2[10]), .B1(in_2[9]), .B0(in_2[8]),
    .A3(A[11]), .A2(A[10]), .A1(A[9]), .A0(A[8]), .S3(out_4[11]), .S2(out_4[10]), .S1(out_4[9]), .S0(out_4[8]));
  FA4 fa4_3 (
    .Cout(fa4_3_cout), .Cin(fa4_4_cout), .B3(in_2[7]), .B2(in_2[6]), .B1(in_2[5]), .B0(in_2[4]), .A3(A[7]),
    .A2(A[6]), .A1(A[5]), .A0(A[4]), .S3(out_4[7]), .S2(out_4[6]), .S1(out_4[5]), .S0(out_4[4]));
  FA4 fa4_4 (
    .Cout(fa4_4_cout), .Cin(1'b0), .B3(in_2[3]), .B2(in_2[2]), .B1(in_2[1]), .B0(in_2[0]), .A3(A[3]),
    .A2(A[2]), .A1(A[1]), .A0(A[0]), .S3(out_4[3]), .S2(out_4[2]), .S1(out_4[1]), .S0(out_4[0]));

  // Notes on the sheet:
  //   B[15:0]
  //   S
  //   Cin
endmodule

module AddSub16 (
  input  [15:0] in_1,
  input  [15:0] in_2,
  output Borrow,
  output [15:0] out_4
);

  wire fa4_1_cout, fa4_2_cout, fa4_3_cout, fa4_4_cout, xor16_1_out_18, xor16_1_out_19, xor16_1_out_20,
       xor16_1_out_21, xor16_1_out_22, xor16_1_out_23, xor16_1_out_24, xor16_1_out_25, xor16_1_out_26,
       xor16_1_out_27, xor16_1_out_28, xor16_1_out_29, xor16_1_out_30, xor16_1_out_31, xor16_1_out_32,
       xor16_1_out_33;

  // Probe on in_2
  not not_1 (Borrow, fa4_1_cout);
  FA4 fa4_1 (
    .Cout(fa4_1_cout), .Cin(fa4_2_cout), .B3(in_2[15]), .B2(in_2[14]), .B1(in_2[13]), .B0(in_2[12]),
    .A3(xor16_1_out_33), .A2(xor16_1_out_32), .A1(xor16_1_out_31), .A0(xor16_1_out_30), .S3(out_4[15]),
    .S2(out_4[14]), .S1(out_4[13]), .S0(out_4[12]));
  FA4 fa4_2 (
    .Cout(fa4_2_cout), .Cin(fa4_3_cout), .B3(in_2[11]), .B2(in_2[10]), .B1(in_2[9]), .B0(in_2[8]),
    .A3(xor16_1_out_29), .A2(xor16_1_out_28), .A1(xor16_1_out_27), .A0(xor16_1_out_26), .S3(out_4[11]),
    .S2(out_4[10]), .S1(out_4[9]), .S0(out_4[8]));
  // Probe on out_4
  // Probe on in_1
  XOR16 xor16_1 (
    .B0(in_1[0]), .B1(in_1[1]), .B2(in_1[2]), .B3(in_1[3]), .B4(in_1[4]), .B5(in_1[5]), .B6(in_1[6]),
    .B7(in_1[7]), .EN(1'b1), .B8(in_1[8]), .B9(in_1[9]), .B10(in_1[10]), .B11(in_1[11]), .B12(in_1[12]),
    .B13(in_1[13]), .B14(in_1[14]), .B15(in_1[15]), .out_18(xor16_1_out_18), .out_19(xor16_1_out_19),
    .out_20(xor16_1_out_20), .out_21(xor16_1_out_21), .out_22(xor16_1_out_22), .out_23(xor16_1_out_23),
    .out_24(xor16_1_out_24), .out_25(xor16_1_out_25), .out_26(xor16_1_out_26), .out_27(xor16_1_out_27),
    .out_28(xor16_1_out_28), .out_29(xor16_1_out_29), .out_30(xor16_1_out_30), .out_31(xor16_1_out_31),
    .out_32(xor16_1_out_32), .out_33(xor16_1_out_33));
  FA4 fa4_3 (
    .Cout(fa4_3_cout), .Cin(fa4_4_cout), .B3(in_2[7]), .B2(in_2[6]), .B1(in_2[5]), .B0(in_2[4]),
    .A3(xor16_1_out_25), .A2(xor16_1_out_24), .A1(xor16_1_out_23), .A0(xor16_1_out_22), .S3(out_4[7]),
    .S2(out_4[6]), .S1(out_4[5]), .S0(out_4[4]));
  FA4 fa4_4 (
    .Cout(fa4_4_cout), .Cin(1'b1), .B3(in_2[3]), .B2(in_2[2]), .B1(in_2[1]), .B0(in_2[0]),
    .A3(xor16_1_out_21), .A2(xor16_1_out_20), .A1(xor16_1_out_19), .A0(xor16_1_out_18), .S3(out_4[3]),
    .S2(out_4[2]), .S1(out_4[1]), .S0(out_4[0]));

  // Notes on the sheet:
  //   A
  //   B
  //   Sum (A+B) or Diff (A-B)
  //   Cin
  //   Add/sub
  //   Sum for Add/Sub=0, Diff for Add/Sub=1
endmodule

module XOR16 (
  input  B0,
  input  B1,
  input  B2,
  input  B3,
  input  B4,
  input  B5,
  input  B6,
  input  B7,
  input  B8,
  input  B9,
  input  B10,
  input  B11,
  input  B12,
  input  B13,
  input  B14,
  input  B15,
  input  EN,
  output out_18,
  output out_19,
  output out_20,
  output out_21,
  output out_22,
  output out_23,
  output out_24,
  output out_25,
  output out_26,
  output out_27,
  output out_28,
  output out_29,
  output out_30,
  output out_31,
  output out_32,
  output out_33
);

  XOR xor_1 (.A(B0), .B(EN), .Y_XOR(out_18));
  XOR xor_2 (.A(B1), .B(EN), .Y_XOR(out_19));
  XOR xor_3 (.A(B2), .B(EN), .Y_XOR(out_20));
  XOR xor_4 (.A(B3), .B(EN), .Y_XOR(out_21));
  XOR xor_5 (.A(B4), .B(EN), .Y_XOR(out_22));
  XOR xor_6 (.A(B5), .B(EN), .Y_XOR(out_23));
  XOR xor_7 (.A(B6), .B(EN), .Y_XOR(out_24));
  XOR xor_8 (.A(B7), .B(EN), .Y_XOR(out_25));
  XOR xor_9 (.A(B8), .B(EN), .Y_XOR(out_26));
  XOR xor_10 (.A(B9), .B(EN), .Y_XOR(out_27));
  XOR xor_11 (.A(B10), .B(EN), .Y_XOR(out_28));
  XOR xor_12 (.A(B11), .B(EN), .Y_XOR(out_29));
  XOR xor_13 (.A(B12), .B(EN), .Y_XOR(out_30));
  XOR xor_14 (.A(B13), .B(EN), .Y_XOR(out_31));
  XOR xor_15 (.A(B14), .B(EN), .Y_XOR(out_32));
  XOR xor_16 (.A(B15), .B(EN), .Y_XOR(out_33));
endmodule

module ShiftL2 (
  input  B0,
  input  B1,
  input  B2,
  input  B3,
  input  B4,
  input  B5,
  input  B6,
  input  B7,
  input  B8,
  input  B9,
  input  B10,
  input  B11,
  input  B12,
  input  B13,
  input  B14,
  input  B15,
  output out_17,
  output out_18,
  output out_19,
  output out_20,
  output out_21,
  output out_22,
  output out_23,
  output out_24,
  output out_25,
  output out_26,
  output out_27,
  output out_28,
  output out_29,
  output out_30,
  output out_31,
  output out_32
);


  assign out_17 = 1'b0;
  assign out_18 = 1'b0;
  assign out_19 = B0;
  assign out_20 = B1;
  assign out_21 = B2;
  assign out_22 = B3;
  assign out_23 = B4;
  assign out_24 = B5;
  assign out_25 = B6;
  assign out_26 = B7;
  assign out_27 = B8;
  assign out_28 = B9;
  assign out_29 = B10;
  assign out_30 = B11;
  assign out_31 = B12;
  assign out_32 = B13;
endmodule

module Mul5add16 (
  input  [15:0] in_1,
  input  [15:0] in_2,
  output [15:0] out_3,
  output out_4
);

  wire [15:0] shiftl2_1_out_17, sum16_1_out_4;

  // Probe on in_1
  // Probe on in_2
  // Probe on sum16_1_out_4
  Sum16 sum16_1 (.A(in_1), .in_2(in_2), .out_4(sum16_1_out_4));  // open: Cout
  ShiftL2 shiftl2_1 (
    .out_17(shiftl2_1_out_17[0]), .out_18(shiftl2_1_out_17[1]), .out_19(shiftl2_1_out_17[2]),
    .out_20(shiftl2_1_out_17[3]), .out_21(shiftl2_1_out_17[4]), .out_22(shiftl2_1_out_17[5]),
    .out_23(shiftl2_1_out_17[6]), .out_24(shiftl2_1_out_17[7]), .out_25(shiftl2_1_out_17[8]),
    .out_26(shiftl2_1_out_17[9]), .out_27(shiftl2_1_out_17[10]), .out_28(shiftl2_1_out_17[11]),
    .out_29(shiftl2_1_out_17[12]), .out_30(shiftl2_1_out_17[13]), .out_31(shiftl2_1_out_17[14]),
    .out_32(shiftl2_1_out_17[15]), .B0(sum16_1_out_4[0]), .B1(sum16_1_out_4[1]), .B2(sum16_1_out_4[2]),
    .B3(sum16_1_out_4[3]), .B4(sum16_1_out_4[4]), .B5(sum16_1_out_4[5]), .B6(sum16_1_out_4[6]),
    .B7(sum16_1_out_4[7]), .B8(sum16_1_out_4[8]), .B9(sum16_1_out_4[9]), .B10(sum16_1_out_4[10]),
    .B11(sum16_1_out_4[11]), .B12(sum16_1_out_4[12]), .B13(sum16_1_out_4[13]), .B14(sum16_1_out_4[14]),
    .B15(sum16_1_out_4[15]));
  Sum16 sum16_2 (.A(shiftl2_1_out_17), .in_2(sum16_1_out_4), .Cout(out_4), .out_4(out_3));
  // Probe on out_3

  // Notes on the sheet:
  //   A
  //   B
  //   Cin
  //   Cout
  //   Cout
  //   Cout
endmodule

module MUX2t1 (
  input  D0,
  input  D1,
  input  S,
  output Y
);

  wire nand_1_y__ab__prime, nand_2_y__ab__prime, nor_1_y___a_b__prime, not_1_x_prime, not_2_x_prime,
       not_3_x_prime;

  NOT not_1 (.X(S), .X_prime(not_1_x_prime));
  NAND nand_1 (.A(D0), .B(not_1_x_prime), .Y__AB__prime(nand_1_y__ab__prime));
  NAND nand_2 (.A(D1), .B(S), .Y__AB__prime(nand_2_y__ab__prime));
  NOT not_2 (.X(nand_1_y__ab__prime), .X_prime(not_2_x_prime));
  NOT not_3 (.X(nand_2_y__ab__prime), .X_prime(not_3_x_prime));
  NOR nor_1 (.A(not_2_x_prime), .B(not_3_x_prime), .Y___A_B__prime(nor_1_y___a_b__prime));
  NOT not_4 (.X(nor_1_y___a_b__prime), .X_prime(Y));
endmodule

module CSA4 (
  input  in_1,
  input  in_2,
  input  in_3,
  input  in_4,
  input  in_5,
  input  in_6,
  input  in_7,
  input  in_8,
  input  Cin,
  output out_10,
  output out_11,
  output out_12,
  output out_13,
  output out_14
);

  wire fa_1_cout, fa_2_cout, fa_3_cout, fa_4_cout, nand_1_y__ab__prime, nand_2_y__ab__prime,
       nand_3_y__ab__prime, not_1_x_prime, not_2_x_prime, not_3_x_prime, xor_1_y_xor, xor_2_y_xor,
       xor_3_y_xor, xor_4_y_xor;

  NOT not_1 (.X(nand_1_y__ab__prime), .X_prime(not_1_x_prime));
  NAND nand_1 (.A(not_3_x_prime), .B(not_2_x_prime), .Y__AB__prime(nand_1_y__ab__prime));
  MUX2t1 mux2t1_1 (.D0(fa_1_cout), .D1(Cin), .S(not_1_x_prime), .Y(out_10));
  NOT not_2 (.X(nand_2_y__ab__prime), .X_prime(not_2_x_prime));
  NAND nand_2 (.A(xor_2_y_xor), .B(xor_1_y_xor), .Y__AB__prime(nand_2_y__ab__prime));
  NAND nand_3 (.A(xor_4_y_xor), .B(xor_3_y_xor), .Y__AB__prime(nand_3_y__ab__prime));
  NOT not_3 (.X(nand_3_y__ab__prime), .X_prime(not_3_x_prime));
  XOR xor_1 (.A(in_2), .B(in_1), .Y_XOR(xor_1_y_xor));
  FA fa_1 (.A(in_1), .B(in_2), .Cin(fa_2_cout), .S(out_11), .Cout(fa_1_cout));
  XOR xor_2 (.A(in_4), .B(in_3), .Y_XOR(xor_2_y_xor));
  FA fa_2 (.A(in_3), .B(in_4), .Cin(fa_3_cout), .S(out_12), .Cout(fa_2_cout));
  XOR xor_3 (.A(in_6), .B(in_5), .Y_XOR(xor_3_y_xor));
  FA fa_3 (.A(in_5), .B(in_6), .Cin(fa_4_cout), .S(out_13), .Cout(fa_3_cout));
  XOR xor_4 (.A(in_8), .B(in_7), .Y_XOR(xor_4_y_xor));
  FA fa_4 (.A(in_7), .B(in_8), .Cin(Cin), .S(out_14), .Cout(fa_4_cout));
endmodule

module AND (
  input  in_1,
  input  in_2,
  output out_3
);

  wire nand_1_y__ab__prime;

  NAND nand_1 (.A(in_1), .B(in_2), .Y__AB__prime(nand_1_y__ab__prime));
  and and_1 (out_3, in_1, in_2);
  NOT not_1 (.X(nand_1_y__ab__prime));  // open: X_prime
endmodule

module MUL4 (
  input  [3:0] B,
  input  [3:0] A,
  output out_3,
  output [7:0] Product
);

  wire csa_1_cout, csa_1_cout_2, csa_1_cout_3, csa_1_cout_4, csa_1_sout, csa_1_sout_2, csa_1_sout_3,
       csa_2_cout, csa_2_cout_2, csa_2_cout_3, csa_2_cout_4, csa_2_sout, csa_2_sout_2, csa_2_sout_3,
       csa_3_cout, csa_3_cout_2, csa_3_cout_3, csa_3_cout_4, csa_3_sout, csa_3_sout_2, csa_3_sout_3,
       csa_4_cout, csa_4_cout_2, csa_4_cout_3, csa_4_cout_4, csa_4_sout, csa_4_sout_2, csa_4_sout_3;

  // Probe on B
  // Probe on A
  CSA csa_1 (
    .Sin(1'b0), .Sin_2(csa_3_sout), .Sin_3(csa_3_sout_2), .Sin_4(csa_3_sout_3), .Cin(csa_3_cout),
    .Cin_2(csa_3_cout_2), .Cin_3(csa_3_cout_3), .Cin_4(csa_3_cout_4), .A(A[3]), .B(B[2]), .A_2(A[2]),
    .B_2(B[2]), .A_3(A[1]), .B_3(B[2]), .A_4(A[0]), .B_4(B[2]), .Cout(csa_1_cout), .Sout(csa_1_sout),
    .Cout_2(csa_1_cout_2), .Sout_2(csa_1_sout_2), .Cout_3(csa_1_cout_3), .Sout_3(csa_1_sout_3),
    .Cout_4(csa_1_cout_4), .Sout_4(Product[2]));
  CPA4 cpa4_1 (
    .Cout(out_3), .Cin(1'b0), .B3(csa_4_cout), .B2(csa_4_cout_2), .B1(csa_4_cout_3), .B0(csa_4_cout_4),
    .A3(1'b0), .A2(csa_4_sout), .A1(csa_4_sout_2), .A0(csa_4_sout_3), .S3(Product[7]), .S2(Product[6]),
    .S1(Product[5]), .S0(Product[4]));
  // Probe on Product
  CSA csa_2 (
    .Sin(1'b0), .Sin_2(1'b0), .Sin_3(1'b0), .Sin_4(1'b0), .Cin(1'b0), .Cin_2(1'b0), .Cin_3(1'b0),
    .Cin_4(1'b0), .A(A[3]), .B(B[0]), .A_2(A[2]), .B_2(B[0]), .A_3(A[1]), .B_3(B[0]), .A_4(A[0]), .B_4(B[0]),
    .Cout(csa_2_cout), .Sout(csa_2_sout), .Cout_2(csa_2_cout_2), .Sout_2(csa_2_sout_2),
    .Cout_3(csa_2_cout_3), .Sout_3(csa_2_sout_3), .Cout_4(csa_2_cout_4), .Sout_4(Product[0]));
  CSA csa_3 (
    .Sin(1'b0), .Sin_2(csa_2_sout), .Sin_3(csa_2_sout_2), .Sin_4(csa_2_sout_3), .Cin(csa_2_cout),
    .Cin_2(csa_2_cout_2), .Cin_3(csa_2_cout_3), .Cin_4(csa_2_cout_4), .A(A[3]), .B(B[1]), .A_2(A[2]),
    .B_2(B[1]), .A_3(A[1]), .B_3(B[1]), .A_4(A[0]), .B_4(B[1]), .Cout(csa_3_cout), .Sout(csa_3_sout),
    .Cout_2(csa_3_cout_2), .Sout_2(csa_3_sout_2), .Cout_3(csa_3_cout_3), .Sout_3(csa_3_sout_3),
    .Cout_4(csa_3_cout_4), .Sout_4(Product[1]));
  CSA csa_4 (
    .Sin(1'b0), .Sin_2(csa_1_sout), .Sin_3(csa_1_sout_2), .Sin_4(csa_1_sout_3), .Cin(csa_1_cout),
    .Cin_2(csa_1_cout_2), .Cin_3(csa_1_cout_3), .Cin_4(csa_1_cout_4), .A(A[3]), .B(B[3]), .A_2(A[2]),
    .B_2(B[3]), .A_3(A[1]), .B_3(B[3]), .A_4(A[0]), .B_4(B[3]), .Cout(csa_4_cout), .Sout(csa_4_sout),
    .Cout_2(csa_4_cout_2), .Sout_2(csa_4_sout_2), .Cout_3(csa_4_cout_3), .Sout_3(csa_4_sout_3),
    .Cout_4(csa_4_cout_4), .Sout_4(Product[3]));
endmodule

module ShiftRegb4 (
  input  D0,
  input  D1,
  input  D2,
  input  D3,
  input  in_5,
  input  Shift_Loadb,
  output Q3,
  output Q2,
  output Q1,
  output Q0
);

  wire and_1_out, and_2_out, and_3_out, and_4_out, and_5_out, and_6_out, and_7_out, and_8_out, clock_1_out,
       not_1_out, not_2_out, not_3_out, not_4_out, not_5_out, or_1_out, or_2_out, or_3_out, or_4_out;

  not not_1 (not_1_out, in_5);
  not not_2 (not_2_out, Shift_Loadb);
  not not_3 (not_3_out, Shift_Loadb);
  not not_4 (not_4_out, Shift_Loadb);
  not not_5 (not_5_out, Shift_Loadb);
  and and_1 (and_1_out, D0, not_1_out, not_2_out);
  and and_2 (and_2_out, Shift_Loadb, 1'b0);
  and and_3 (and_3_out, D1, not_1_out, not_3_out);
  and and_4 (and_4_out, Shift_Loadb, Q3);
  and and_5 (and_5_out, D2, not_1_out, not_4_out);
  and and_6 (and_6_out, Shift_Loadb, Q2);
  and and_7 (and_7_out, D3, not_1_out, not_5_out);
  and and_8 (and_8_out, Shift_Loadb, Q1);
  Clock clock_1 (.out(clock_1_out));
  or or_1 (or_1_out, and_1_out, and_2_out);
  or or_2 (or_2_out, and_3_out, and_4_out);
  or or_3 (or_3_out, and_5_out, and_6_out);
  or or_4 (or_4_out, and_7_out, and_8_out);
  D_Flip_Flop d_ff_1 (.clk(clock_1_out), .D(or_1_out), .Q(Q3), .en(1'b1));  // open: Qn, preset, reset
  D_Flip_Flop d_ff_2 (.clk(clock_1_out), .D(or_2_out), .Q(Q2), .en(1'b1));  // open: Qn, preset, reset
  D_Flip_Flop d_ff_3 (.clk(clock_1_out), .D(or_3_out), .Q(Q1), .en(1'b1));  // open: Qn, preset, reset
  D_Flip_Flop d_ff_4 (.clk(clock_1_out), .D(or_4_out), .Q(Q0), .en(1'b1));  // open: Qn, preset, reset

  // Notes on the sheet:
  //   Clear when load enable (0)
  //   Right shift
endmodule

module ShiftAddMul4 (
  input  [3:0] in_1,
  input  [3:0] in_2,
  input  strt,
  input  in_4,
  input  in_5,
  output [7:0] out_6
);

  wire clock_1_out, counter_1_carry, fa4_1_s0, fa4_1_s1, fa4_1_s2, fa4_1_s3, mux2t1_1_y, mux2t1_2_y,
       mux2t1_3_y, mux2t1_4_y, not_1_out, or_1_out, shift_register_1_out, t_ff_1_q, t_ff_1_qn;
  wire [2:0] counter_1_q;
  wire [3:0] multiplexer_1_out;
  wire [7:0] shift_register_1_q3;

  MUX2t1 mux2t1_1 (.D0(1'b0), .D1(in_1[3]), .S(shift_register_1_q3[0]), .Y(mux2t1_1_y));
  not not_1 (not_1_out, strt);
  or or_1 (or_1_out, strt, t_ff_1_q);
  Counter #(.width(3), .max('h7)) counter_1 (
    .load(1'b0), .D(3'b000), .count(1'b1), .Q(counter_1_q), .carry(counter_1_carry), .clk(clock_1_out),
    .clr(strt));
  // Probe on in_1
  MUX2t1 mux2t1_2 (.D0(1'b0), .D1(in_1[2]), .S(shift_register_1_q3[0]), .Y(mux2t1_2_y));
  FA4 fa4_1 (
    .Cin(1'b0), .B3(shift_register_1_q3[7]), .B2(shift_register_1_q3[6]), .B1(shift_register_1_q3[5]),
    .B0(shift_register_1_q3[4]), .A3(mux2t1_1_y), .A2(mux2t1_2_y), .A1(mux2t1_3_y), .A0(mux2t1_4_y),
    .S3(fa4_1_s3), .S2(fa4_1_s2), .S1(fa4_1_s1), .S0(fa4_1_s0));  // open: Cout
  Clock clock_1 (.out(clock_1_out));
  // Probe on counter_1_q
  // Probe on counter_1_carry
  MUX2t1 mux2t1_3 (.D0(1'b0), .D1(in_1[1]), .S(shift_register_1_q3[0]), .Y(mux2t1_3_y));
  Shift_Register shift_register_1 (
    .shift(t_ff_1_qn), .in(1'b0), .clk(clock_1_out), .out(shift_register_1_out), .load(or_1_out), .clr(1'b0),
    .d0(fa4_1_s3), .q0(shift_register_1_q3[7]), .d1(fa4_1_s2), .q1(shift_register_1_q3[6]), .d2(fa4_1_s1),
    .q2(shift_register_1_q3[5]), .d3(fa4_1_s0), .q3(shift_register_1_q3[4]), .d4(multiplexer_1_out[3]),
    .q4(shift_register_1_q3[3]), .d5(multiplexer_1_out[2]), .q5(shift_register_1_q3[2]),
    .d6(multiplexer_1_out[1]), .q6(shift_register_1_q3[1]), .d7(multiplexer_1_out[0]),
    .q7(shift_register_1_q3[0]));
  // Probe on out_6
  Register register_1 (.D(shift_register_1_q3), .en(counter_1_carry), .Q(out_6), .clk(clock_1_out), .clr(1'b0));
  // Probe on shift_register_1_q3
  T_Flip_Flop t_ff_1 (
    .clk(clock_1_out), .T(1'b1), .Q(t_ff_1_q), .Qn(t_ff_1_qn), .preset(1'b0), .reset(1'b0), .en(1'b1));
  MUX2t1 mux2t1_4 (.D0(1'b0), .D1(in_1[0]), .S(shift_register_1_q3[0]), .Y(mux2t1_4_y));
  // Probe on shift_register_1_out
  // Probe on in_2
  Multiplexer #(.width(4)) multiplexer_1 (
    .in0(in_2), .in1(shift_register_1_q3[3:0]), .out(multiplexer_1_out), .sel(not_1_out), .en(1'b1));
endmodule

module ShiftAddMul16 (
  input  [15:0] A,
  input  [15:0] B,
  input  strt,
  input  Rst,
  input  in_5,
  input  in_6,
  output [31:0] out_7
);

  wire clock_1_out, counter_1_carry, d_ff_1_q, d_ff_1_qn, not_1_out, or_1_out, shift_register_1_out,
       t_ff_1_q, t_ff_1_qn, xor_1_out;
  wire [3:0] counter_1_q;
  wire [15:0] multiplexer_1_out, mux2t1b16_1_out_4, shift_register_1_q15, sum16_1_out_4;
  wire [31:0] shift_register_1_q0;

  not not_1 (not_1_out, strt);
  or or_1 (or_1_out, strt, d_ff_1_q);
  Counter #(.width(4), .max('hf)) counter_1 (
    .load(1'b0), .D(4'b0000), .count(1'b1), .Q(counter_1_q), .carry(counter_1_carry), .clk(clock_1_out),
    .clr(strt));
  // Probe on A
  Clock clock_1 (.out(clock_1_out));
  // Probe on counter_1_q
  // Probe on counter_1_carry
  MUX2t1b16 mux2t1b16_1 (.in_1({16{1'b0}}), .in_2(A), .in_3(shift_register_1_q0[0]), .out_4(mux2t1b16_1_out_4));
  Sum16 sum16_1 (
    .A(mux2t1b16_1_out_4),
    .in_2({shift_register_1_q15[15:5], shift_register_1_q15[5], shift_register_1_q15[3:0]}),
    .out_4(sum16_1_out_4));  // open: Cout
  Shift_Register #(.length(32)) shift_register_1 (
    .shift(d_ff_1_qn), .in(1'b0), .clk(clock_1_out), .out(shift_register_1_out), .load(or_1_out), .clr(Rst),
    .d0(sum16_1_out_4[15]), .q0(shift_register_1_q0[31]), .d1(sum16_1_out_4[14]),
    .q1(shift_register_1_q15[15]), .d2(sum16_1_out_4[13]), .q2(shift_register_1_q15[14]),
    .d3(sum16_1_out_4[12]), .q3(shift_register_1_q15[13]), .d4(sum16_1_out_4[11]),
    .q4(shift_register_1_q15[12]), .d5(sum16_1_out_4[10]), .q5(shift_register_1_q15[11]),
    .d6(sum16_1_out_4[9]), .q6(shift_register_1_q15[10]), .d7(sum16_1_out_4[8]),
    .q7(shift_register_1_q15[9]), .d8(sum16_1_out_4[7]), .q8(shift_register_1_q15[8]), .d9(sum16_1_out_4[6]),
    .q9(shift_register_1_q15[7]), .d10(sum16_1_out_4[5]), .q10(shift_register_1_q15[6]),
    .d11(sum16_1_out_4[4]), .q11(shift_register_1_q15[5]), .d12(sum16_1_out_4[3]),
    .q12(shift_register_1_q15[3]), .d13(sum16_1_out_4[2]), .q13(shift_register_1_q15[2]),
    .d14(sum16_1_out_4[1]), .q14(shift_register_1_q15[1]), .d15(sum16_1_out_4[0]),
    .q15(shift_register_1_q15[0]), .d16(multiplexer_1_out[15]), .q16(shift_register_1_q0[15]),
    .d17(multiplexer_1_out[14]), .q17(shift_register_1_q0[14]), .d18(multiplexer_1_out[13]),
    .q18(shift_register_1_q0[13]), .d19(multiplexer_1_out[12]), .q19(shift_register_1_q0[12]),
    .d20(multiplexer_1_out[11]), .q20(shift_register_1_q0[11]), .d21(multiplexer_1_out[10]),
    .q21(shift_register_1_q0[10]), .d22(multiplexer_1_out[9]), .q22(shift_register_1_q0[9]),
    .d23(multiplexer_1_out[8]), .q23(shift_register_1_q0[8]), .d24(multiplexer_1_out[7]),
    .q24(shift_register_1_q0[7]), .d25(multiplexer_1_out[6]), .q25(shift_register_1_q0[6]),
    .d26(multiplexer_1_out[5]), .q26(shift_register_1_q0[5]), .d27(multiplexer_1_out[4]),
    .q27(shift_register_1_q0[4]), .d28(multiplexer_1_out[3]), .q28(shift_register_1_q0[3]),
    .d29(multiplexer_1_out[2]), .q29(shift_register_1_q0[2]), .d30(multiplexer_1_out[1]),
    .q30(shift_register_1_q0[1]), .d31(multiplexer_1_out[0]), .q31(shift_register_1_q0[0]));
  Register #(.width(32)) register_1 (
    .D({shift_register_1_q0[31], shift_register_1_q15[15:5], shift_register_1_q15[3:0], shift_register_1_q0[15:0]}),
    .en(counter_1_carry), .Q(out_7), .clk(clock_1_out), .clr(1'b0));
  // Probe on {shift_register_1_q0[31], shift_register_1_q15[15:5], shift_register_1_q15[3:0], shift_register_1_q0[15:0]}
  T_Flip_Flop t_ff_1 (
    .clk(clock_1_out), .T(1'b1), .Q(t_ff_1_q), .Qn(t_ff_1_qn), .preset(1'b0), .reset(1'b0), .en(1'b1));
  // Probe on out_7
  xor xor_1 (xor_1_out, d_ff_1_q, 1'b1);
  // Probe on shift_register_1_out
  D_Flip_Flop d_ff_1 (
    .clk(clock_1_out), .D(xor_1_out), .Q(d_ff_1_q), .Qn(d_ff_1_qn), .en(1'b1));  // open: preset, reset
  // Probe on B
  Multiplexer #(.width(16)) multiplexer_1 (
    .in0(B), .in1(shift_register_1_q0[15:0]), .out(multiplexer_1_out), .sel(not_1_out), .en(1'b1));

  // Notes on the sheet:
  //   strt: pull=down
  //   output results in 16 clock cycles (32 clock transitions)
  //   this register currently gives second last value, add one more clock cycle
  //   first Rst pulse then Strt high then pass one clock cycle to load inputs then Strt low then toggle clock 32 times
endmodule

module DLatch (
  input  D,
  input  Clk,
  output Q,
  output Q_prime
);

  wire nand_1_y__ab__prime, nand_2_y__ab__prime, not_1_x_prime;

  NOT not_1 (.X(D), .X_prime(not_1_x_prime));
  NAND nand_1 (.A(D), .B(Clk), .Y__AB__prime(nand_1_y__ab__prime));
  NAND nand_2 (.A(not_1_x_prime), .B(Clk), .Y__AB__prime(nand_2_y__ab__prime));
  nand nand_3 (Q, nand_1_y__ab__prime, Q_prime);
  nand nand_4 (Q_prime, Q, nand_2_y__ab__prime);
endmodule

module DFlipFlop (
  input  in_1,
  output out_2
);

  wire clock_1_out, dlatch_1_q, not_1_out, not_2_out;

  Clock clock_1 (.out(clock_1_out));
  not not_1 (not_1_out, clock_1_out);
  DLatch dlatch_1 (.D(in_1), .Clk(not_1_out), .Q(dlatch_1_q));  // open: Q_prime
  not not_2 (not_2_out, not_1_out);
  DLatch dlatch_2 (.D(dlatch_1_q), .Clk(not_2_out), .Q(out_2));  // open: Q_prime
endmodule

module MUX4t1 (
  input  I0,
  input  I1,
  input  I2,
  input  I3,
  input  S0,
  input  S1,
  output Out
);

  wire mux2t1_1_y, mux2t1_2_y;

  MUX2t1 mux2t1_1 (.D0(I0), .D1(I1), .S(S0), .Y(mux2t1_1_y));
  MUX2t1 mux2t1_2 (.D0(I2), .D1(I3), .S(S0), .Y(mux2t1_2_y));
  MUX2t1 mux2t1_3 (.D0(mux2t1_1_y), .D1(mux2t1_2_y), .S(S1), .Y(Out));
endmodule

module MUX4t1b4 (
  input  [3:0] in_1,
  input  [3:0] in_2,
  input  [3:0] in_3,
  input  [3:0] in_4,
  input  S1,
  input  S0,
  output [3:0] out_7
);

  // Probe on in_1
  // Probe on in_2
  // Probe on in_3
  // Probe on in_4
  MUX4t1 mux4t1_1 (.I0(in_1[0]), .I1(in_2[0]), .I2(in_3[0]), .I3(in_4[0]), .S0(S0), .S1(S1), .Out(out_7[0]));
  MUX4t1 mux4t1_2 (.I0(in_1[1]), .I1(in_2[1]), .I2(in_3[1]), .I3(in_4[1]), .S0(S0), .S1(S1), .Out(out_7[1]));
  MUX4t1 mux4t1_3 (.I0(in_1[2]), .I1(in_2[2]), .I2(in_3[2]), .I3(in_4[2]), .S0(S0), .S1(S1), .Out(out_7[2]));
  MUX4t1 mux4t1_4 (.I0(in_1[3]), .I1(in_2[3]), .I2(in_3[3]), .I3(in_4[3]), .S0(S0), .S1(S1), .Out(out_7[3]));
  // Probe on out_7
endmodule

module MUX4t1b16 (
  input  [15:0] in_1,
  input  [15:0] in_2,
  input  [15:0] in_3,
  input  [15:0] in_4,
  input  S1,
  input  S0,
  output [15:0] out_7
);

  // Probe on in_1
  // Probe on in_2
  // Probe on in_3
  // Probe on in_4
  MUX4t1b4 mux4t1b4_1 (
    .in_1(in_1[3:0]), .in_2(in_2[3:0]), .in_3(in_3[3:0]), .in_4(in_4[3:0]), .out_7(out_7[3:0]), .S1(S1),
    .S0(S0));
  MUX4t1b4 mux4t1b4_2 (
    .in_1(in_1[7:4]), .in_2(in_2[7:4]), .in_3(in_3[7:4]), .in_4(in_4[7:4]), .out_7(out_7[7:4]), .S1(S1),
    .S0(S0));
  MUX4t1b4 mux4t1b4_3 (
    .in_1(in_1[11:8]), .in_2(in_2[11:8]), .in_3(in_3[11:8]), .in_4(in_4[11:8]), .out_7(out_7[11:8]), .S1(S1),
    .S0(S0));
  MUX4t1b4 mux4t1b4_4 (
    .in_1(in_1[15:12]), .in_2(in_2[15:12]), .in_3(in_3[15:12]), .in_4(in_4[15:12]), .out_7(out_7[15:12]),
    .S1(S1), .S0(S0));
  // Probe on out_7
endmodule

module MUX4t1b32 (
  input  [31:0] in_1,
  input  [31:0] in_2,
  input  [31:0] in_3,
  input  [31:0] in_4,
  input  in_5,
  input  in_6,
  output [31:0] out_7
);

  MUX4t1b16 mux4t1b16_1 (
    .in_1(in_1[15:0]), .in_2(in_2[15:0]), .in_3(in_3[15:0]), .in_4(in_4[15:0]), .out_7(out_7[15:0]),
    .S1(in_5), .S0(in_6));
  MUX4t1b16 mux4t1b16_2 (
    .in_1(in_1[31:16]), .in_2(in_2[31:16]), .in_3(in_3[31:16]), .in_4(in_4[31:16]), .out_7(out_7[31:16]),
    .S1(in_5), .S0(in_6));
endmodule

module MUX2t1b4 (
  input  [3:0] in_1,
  input  [3:0] in_2,
  input  in_3,
  output [3:0] out_4
);

  // Probe on in_1
  // Probe on in_2
  MUX2t1 mux2t1_1 (.D0(in_1[0]), .D1(in_2[0]), .S(in_3), .Y(out_4[0]));
  MUX2t1 mux2t1_2 (.D0(in_1[1]), .D1(in_2[1]), .S(in_3), .Y(out_4[1]));
  MUX2t1 mux2t1_3 (.D0(in_1[2]), .D1(in_2[2]), .S(in_3), .Y(out_4[2]));
  MUX2t1 mux2t1_4 (.D0(in_1[3]), .D1(in_2[3]), .S(in_3), .Y(out_4[3]));
  // Probe on out_4
endmodule

module MUX2t1b16 (
  input  [15:0] in_1,
  input  [15:0] in_2,
  input  in_3,
  output [15:0] out_4
);

  // Probe on in_1
  // Probe on in_2
  MUX2t1b4 mux2t1b4_1 (.in_1(in_1[3:0]), .in_2(in_2[3:0]), .in_3(in_3), .out_4(out_4[3:0]));
  MUX2t1b4 mux2t1b4_2 (.in_1(in_1[7:4]), .in_2(in_2[7:4]), .in_3(in_3), .out_4(out_4[7:4]));
  MUX2t1b4 mux2t1b4_3 (.in_1(in_1[11:8]), .in_2(in_2[11:8]), .in_3(in_3), .out_4(out_4[11:8]));
  MUX2t1b4 mux2t1b4_4 (.in_1(in_1[15:12]), .in_2(in_2[15:12]), .in_3(in_3), .out_4(out_4[15:12]));
  // Probe on out_4
endmodule

module CPA4 (
  input  B3,
  input  B2,
  input  B1,
  input  B0,
  input  A3,
  input  A2,
  input  A1,
  input  A0,
  input  Cin,
  output Cout,
  output S3,
  output S2,
  output S1,
  output S0
);

  wire fa_2_cout, fa_3_cout, fa_4_cout;

  FA fa_1 (.A(A3), .B(B3), .Cin(fa_2_cout), .S(S3), .Cout(Cout));
  FA fa_2 (.A(A2), .B(B2), .Cin(fa_3_cout), .S(S2), .Cout(fa_2_cout));
  FA fa_3 (.A(A1), .B(B1), .Cin(fa_4_cout), .S(S1), .Cout(fa_3_cout));
  FA fa_4 (.A(A0), .B(B0), .Cin(Cin), .S(S0), .Cout(fa_4_cout));

  // Notes on the sheet:
  //   B3: pull=down
  //   B1: pull=down
  //   B0: pull=down
  //   A3: pull=down
  //   B2: pull=down
  //   A0: pull=down
  //   A2: pull=down
  //   A1: pull=down
endmodule

module CPA16 (
  input  [15:0] in_1,
  input  [14:0] in_2,
  input  in_3,
  output out_4,
  output [15:0] out_5
);

  wire cpa4_2_cout, cpa4_3_cout, cpa4_4_cout;

  CPA4 cpa4_1 (
    .Cout(out_4), .Cin(cpa4_2_cout), .B3(in_1[15]), .B2(in_1[14]), .B1(in_1[13]), .B0(in_1[12]), .A3(1'b0),
    .A2(in_2[14]), .A1(in_2[13]), .A0(in_2[12]), .S3(out_5[15]), .S2(out_5[14]), .S1(out_5[13]),
    .S0(out_5[12]));
  CPA4 cpa4_2 (
    .Cout(cpa4_2_cout), .Cin(cpa4_3_cout), .B3(in_1[11]), .B2(in_1[10]), .B1(in_1[9]), .B0(in_1[8]),
    .A3(in_2[11]), .A2(in_2[10]), .A1(in_2[9]), .A0(in_2[8]), .S3(out_5[11]), .S2(out_5[10]), .S1(out_5[9]),
    .S0(out_5[8]));
  CPA4 cpa4_3 (
    .Cout(cpa4_3_cout), .Cin(cpa4_4_cout), .B3(in_1[7]), .B2(in_1[6]), .B1(in_1[5]), .B0(in_1[4]),
    .A3(in_2[7]), .A2(in_2[6]), .A1(in_2[5]), .A0(in_2[4]), .S3(out_5[7]), .S2(out_5[6]), .S1(out_5[5]),
    .S0(out_5[4]));
  CPA4 cpa4_4 (
    .Cout(cpa4_4_cout), .Cin(in_3), .B3(in_1[3]), .B2(in_1[2]), .B1(in_1[1]), .B0(in_1[0]), .A3(in_2[3]),
    .A2(in_2[2]), .A1(in_2[1]), .A0(in_2[0]), .S3(out_5[3]), .S2(out_5[2]), .S1(out_5[1]), .S0(out_5[0]));
endmodule

module CSA (
  input  A,
  input  B,
  input  A_2,
  input  B_2,
  input  A_3,
  input  B_3,
  input  A_4,
  input  B_4,
  input  Sin,
  input  Sin_2,
  input  Sin_3,
  input  Sin_4,
  input  Cin,
  input  Cin_2,
  input  Cin_3,
  input  Cin_4,
  output Cout,
  output Sout,
  output Cout_2,
  output Sout_2,
  output Cout_3,
  output Sout_3,
  output Cout_4,
  output Sout_4
);

  wire and_1_out_3, and_2_out_3, and_3_out_3, and_4_out_3;

  AND and_1 (.in_1(B), .in_2(A), .out_3(and_1_out_3));
  FA fa_1 (.A(and_1_out_3), .B(Sin), .Cin(Cin), .S(Sout), .Cout(Cout));
  AND and_2 (.in_1(B_2), .in_2(A_2), .out_3(and_2_out_3));
  FA fa_2 (.A(and_2_out_3), .B(Sin_2), .Cin(Cin_2), .S(Sout_2), .Cout(Cout_2));
  AND and_3 (.in_1(B_3), .in_2(A_3), .out_3(and_3_out_3));
  FA fa_3 (.A(and_3_out_3), .B(Sin_3), .Cin(Cin_3), .S(Sout_3), .Cout(Cout_3));
  AND and_4 (.in_1(B_4), .in_2(A_4), .out_3(and_4_out_3));
  FA fa_4 (.A(and_4_out_3), .B(Sin_4), .Cin(Cin_4), .S(Sout_4), .Cout(Cout_4));

  // Notes on the sheet:
  //   Cin_4: pull=down
  //   Cin: pull=down
  //   Cin_3: pull=down
  //   Cin_2: pull=down
endmodule

module CSA16 (
  input  B,
  input  [15:0] in_2,
  input  [15:0] in_3,
  input  [14:0] in_4,
  output [15:0] out_5,
  output S0,
  output [14:0] out_7
);

  CSA csa_1 (
    .Sin(1'b0), .Sin_2(in_4[14]), .Sin_3(in_4[13]), .Sin_4(in_4[12]), .Cin(in_3[15]), .Cin_2(in_3[14]),
    .Cin_3(in_3[13]), .Cin_4(in_3[12]), .A(in_2[15]), .B(B), .A_2(in_2[14]), .B_2(B), .A_3(in_2[13]),
    .B_3(B), .A_4(in_2[12]), .B_4(B), .Cout(out_5[15]), .Sout(out_7[14]), .Cout_2(out_5[14]),
    .Sout_2(out_7[13]), .Cout_3(out_5[13]), .Sout_3(out_7[12]), .Cout_4(out_5[12]), .Sout_4(out_7[11]));
  // Probe on out_5
  CSA csa_2 (
    .Sin(in_4[11]), .Sin_2(in_4[10]), .Sin_3(in_4[9]), .Sin_4(in_4[8]), .Cin(in_3[11]), .Cin_2(in_3[10]),
    .Cin_3(in_3[9]), .Cin_4(in_3[8]), .A(in_2[11]), .B(B), .A_2(in_2[10]), .B_2(B), .A_3(in_2[9]), .B_3(B),
    .A_4(in_2[8]), .B_4(B), .Cout(out_5[11]), .Sout(out_7[10]), .Cout_2(out_5[10]), .Sout_2(out_7[9]),
    .Cout_3(out_5[9]), .Sout_3(out_7[8]), .Cout_4(out_5[8]), .Sout_4(out_7[7]));
  CSA csa_3 (
    .Sin(in_4[7]), .Sin_2(in_4[6]), .Sin_3(in_4[5]), .Sin_4(in_4[4]), .Cin(in_3[7]), .Cin_2(in_3[6]),
    .Cin_3(in_3[5]), .Cin_4(in_3[4]), .A(in_2[7]), .B(B), .A_2(in_2[6]), .B_2(B), .A_3(in_2[5]), .B_3(B),
    .A_4(in_2[4]), .B_4(B), .Cout(out_5[7]), .Sout(out_7[6]), .Cout_2(out_5[6]), .Sout_2(out_7[5]),
    .Cout_3(out_5[5]), .Sout_3(out_7[4]), .Cout_4(out_5[4]), .Sout_4(out_7[3]));
  CSA csa_4 (
    .Sin(in_4[3]), .Sin_2(in_4[2]), .Sin_3(in_4[1]), .Sin_4(in_4[0]), .Cin(in_3[3]), .Cin_2(in_3[2]),
    .Cin_3(in_3[1]), .Cin_4(in_3[0]), .A(in_2[3]), .B(B), .A_2(in_2[2]), .B_2(B), .A_3(in_2[1]), .B_3(B),
    .A_4(in_2[0]), .B_4(B), .Cout(out_5[3]), .Sout(out_7[2]), .Cout_2(out_5[2]), .Sout_2(out_7[1]),
    .Cout_3(out_5[1]), .Sout_3(out_7[0]), .Cout_4(out_5[0]), .Sout_4(S0));

  // Notes on the sheet:
  //   Sin
  //   Cout
  //   A
  //   Sout
  //   Cin
endmodule

module CSA16b2 (
  input  [1:0] in_1,
  input  [15:0] in_2,
  input  [14:0] in_3,
  input  [15:0] in_4,
  output [1:0] out_5,
  output [15:0] out_6,
  output [14:0] out_7
);

  wire [14:0] csa16_1_out_7;
  wire [15:0] csa16_1_out_5;

  CSA16 csa16_1 (
    .in_3(in_4), .out_5(csa16_1_out_5), .in_4(in_3), .out_7(csa16_1_out_7), .B(in_1[0]), .in_2(in_2),
    .S0(out_5[0]));
  CSA16 csa16_2 (
    .in_3(csa16_1_out_5), .out_5(out_6), .in_4(csa16_1_out_7), .out_7(out_7), .B(in_1[1]), .in_2(in_2),
    .S0(out_5[1]));

  // Notes on the sheet:
  //   in_2: pull=down
  //   in_4: pull=down
endmodule

module CSA16b4 (
  input  [3:0] in_1,
  input  [15:0] in_2,
  input  [14:0] in_3,
  input  [15:0] in_4,
  output [3:0] out_5,
  output [15:0] out_6,
  output [14:0] out_7
);

  wire [14:0] csa16b2_1_out_7;
  wire [15:0] csa16b2_1_out_6;

  CSA16b2 csa16b2_1 (
    .out_6(csa16b2_1_out_6), .out_7(csa16b2_1_out_7), .in_1(in_1[1:0]), .in_2(in_2), .in_4(in_4),
    .in_3(in_3), .out_5(out_5[1:0]));
  CSA16b2 csa16b2_2 (
    .out_6(out_6), .out_7(out_7), .in_1(in_1[3:2]), .in_2(in_2), .in_4(csa16b2_1_out_6),
    .in_3(csa16b2_1_out_7), .out_5(out_5[3:2]));
endmodule

module CSA16b16 (
  input  [15:0] in_1,
  input  [15:0] in_2,
  output out_3,
  output [31:0] out_4
);

  wire [14:0] csa16b4_1_out_7, csa16b4_2_out_7, csa16b4_3_out_7, csa16b4_4_out_7;
  wire [15:0] csa16b4_1_out_6, csa16b4_2_out_6, csa16b4_3_out_6, csa16b4_4_out_6;

  // Probe on in_1
  CSA16b4 csa16b4_1 (
    .in_3({15{1'b0}}), .out_6(csa16b4_1_out_6), .in_4({16{1'b0}}), .out_7(csa16b4_1_out_7), .in_1(in_1[3:0]),
    .in_2(in_2), .out_5(out_4[3:0]));
  CSA16b4 csa16b4_2 (
    .in_3(csa16b4_1_out_7), .out_6(csa16b4_2_out_6), .in_4(csa16b4_1_out_6), .out_7(csa16b4_2_out_7),
    .in_1(in_1[7:4]), .in_2(in_2), .out_5(out_4[7:4]));
  CSA16b4 csa16b4_3 (
    .in_3(csa16b4_2_out_7), .out_6(csa16b4_3_out_6), .in_4(csa16b4_2_out_6), .out_7(csa16b4_3_out_7),
    .in_1(in_1[11:8]), .in_2(in_2), .out_5(out_4[11:8]));
  CSA16b4 csa16b4_4 (
    .in_3(csa16b4_3_out_7), .out_6(csa16b4_4_out_6), .in_4(csa16b4_3_out_6), .out_7(csa16b4_4_out_7),
    .in_1(in_1[15:12]), .in_2(in_2), .out_5(out_4[15:12]));
  CPA16 cpa16_1 (.out_4(out_3), .in_3(1'b0), .out_5(out_4[31:16]), .in_1(csa16b4_4_out_6), .in_2(csa16b4_4_out_7));
  // Probe on in_2
  // Probe on out_4
  // Probe on out_4[15:0]

  // Notes on the sheet:
  //   in_2: pull=down
  //   in_1: pull=down
endmodule

module Final (
  input  [15:0] in_1,
  input  [15:0] in_2,
  input  S1,
  input  S0,
  output [31:0] out_5,
  output Cout
);

  wire addsub16_1_borrow, csa16b16_1_out_3, mul5add16_1_out_4, undriven;
  wire [15:0] addsub16_1_out_4, mul5add16_1_out_3;
  wire [31:0] csa16b16_1_out_4, shiftaddmul16_1_out_7;

  CSA16b16 csa16b16_1 (.out_3(csa16b16_1_out_3), .out_4(csa16b16_1_out_4), .in_1(in_2), .in_2(in_1));
  ShiftAddMul16 shiftaddmul16_1 (
    .in_5(undriven), .A(in_2), .B(in_1), .out_7(shiftaddmul16_1_out_7));  // open: strt, in_6, Rst
  AddSub16 addsub16_1 (.Borrow(addsub16_1_borrow), .out_4(addsub16_1_out_4), .in_1(in_2), .in_2(in_1));
  Mul5add16 mul5add16_1 (.in_1(in_1), .in_2(in_2), .out_3(mul5add16_1_out_3), .out_4(mul5add16_1_out_4));
  // Probe on csa16b16_1_out_4
  // Probe on shiftaddmul16_1_out_7
  // Probe on addsub16_1_out_4
  // Probe on mul5add16_1_out_3
  // MUX4t1b32 mux4t1b32_1: pin names not known; wires that end beside it: shiftaddmul16_1_out_7, {{16{1'b0}}, addsub16_1_out_4}, {{16{1'b0}}, mul5add16_1_out_3}, S1, S0, out_5
  // Probe on out_5
  MUX4t1 mux4t1_1 (
    .I0(csa16b16_1_out_3), .I1(undriven), .I2(addsub16_1_borrow), .I3(mul5add16_1_out_4), .S0(S0), .S1(S1),
    .Out(Cout));

  // Notes on the sheet:
  //   A
  //   B
  //   CSA, CPA multiply
  //   ShiftAddMul
  //   A-B
  //   5*(A+B)
  //   Output
endmodule
